// Logisim project 四位可控加减法器.circ as structural Verilog: 8 circuits, main circuit 1-bit FA
// FA
module _1_bit_FA (
  input  a,
  input  b,
  input  c_l,
  output s,
  output c
);

  wire and_1_out, and_2_out, xor_1_out;

  and and_1 (and_1_out, a, b);
  xor xor_1 (xor_1_out, a, b);
  and and_2 (and_2_out, xor_1_out, c_l);
  xor xor_2 (s, xor_1_out, c_l);
  or or_1 (c, and_2_out, and_1_out);

  // Notes on the sheet:
  //   1-bit full adder
endmodule

module OF (
  input  a,
  input  b,
  input  s,
  output out_4
);

  wire and_1_out, and_2_out, not_1_out, not_2_out, not_3_out;

  not not_1 (not_1_out, a);
  not not_2 (not_2_out, b);
  not not_3 (not_3_out, s);
  and and_1 (and_1_out, not_1_out, not_2_out, s);
  and and_2 (and_2_out, a, not_3_out, b);
  or or_1 (out_4, and_1_out, and_2_out);

  // Notes on the sheet:
  //   溢出判断
endmodule

module \_4位快速加法器  (
  input  C0,
  input  X3,
  input  Y3,
  input  X2,
  input  Y2,
  input  X1,
  input  Y1,
  input  X0,
  input  Y0,
  output out_10,
  output C3,
  output S3,
  output S2,
  output S1,
  output S0,
  output G_star,
  output P_star,
  output C4
);

  wire and_1_out, and_2_out, and_3_out, and_4_out, \n4位先行进位电路_cla74182_1_c1 , \n4位先行进位电路_cla74182_1_c2 ,
       xor_1_out, xor_3_out, xor_5_out, xor_7_out;

  OF of_1 (.a(X3), .b(X3), .s(S3), .out_4(out_10));
  and and_1 (and_1_out, X3, X3);
  xor xor_1 (xor_1_out, X3, X3);
  xor xor_2 (S3, C3, xor_1_out);
  xor xor_3 (xor_3_out, X2, Y2);
  and and_2 (and_2_out, X2, Y2);
  xor xor_4 (S2, \n4位先行进位电路_cla74182_1_c2 , xor_3_out);
  xor xor_5 (xor_5_out, X1, Y1);
  and and_3 (and_3_out, X1, Y1);
  xor xor_6 (S1, \n4位先行进位电路_cla74182_1_c1 , xor_5_out);
  and and_4 (and_4_out, X0, Y0);
  xor xor_7 (xor_7_out, X0, Y0);
  xor xor_8 (S0, xor_7_out, C0);
  \_4位先行进位电路_CLA74182  \u_4位先行进位电路_cla74182_1  (
    .Cin(C0), .G1(and_4_out), .P1(xor_7_out), .G2(and_3_out), .P2(xor_5_out), .G3(and_2_out), .P3(xor_3_out),
    .G4(and_1_out), .P4(xor_1_out), .G_star(G_star), .P_star(P_star), .C1(\n4位先行进位电路_cla74182_1_c1 ),
    .C2(\n4位先行进位电路_cla74182_1_c2 ), .C3(C3), .C4(C4));

  assign Y3 = X3;
endmodule

// CLA74182
module \_4位先行进位电路_CLA74182  (
  input  Cin,
  input  G1,
  input  P1,
  input  G2,
  input  P2,
  input  G3,
  input  P3,
  input  G4,
  input  P4,
  output G_star,
  output P_star,
  output C1,
  output C2,
  output C3,
  output C4
);

  wire and_1_out, and_2_out, and_3_out, and_5_out, and_6_out, and_7_out, and_8_out, and_9_out, and_10_out,
       and_11_out, and_12_out, and_13_out, and_14_out, or_3_out;

  and and_1 (and_1_out, P4, G3);
  and and_2 (and_2_out, P4, P3, G2);
  and and_3 (and_3_out, P4, P3, P2, G1);
  and and_4 (P_star, P4, P2, P2, P1);
  and and_5 (and_5_out, P1, Cin);
  and and_6 (and_6_out, P1, Cin);
  and and_7 (and_7_out, P3, G2);
  and and_8 (and_8_out, P3, P2, G1);
  and and_9 (and_9_out, P3, P2, P1, Cin);
  and and_10 (and_10_out, P4, G3);
  and and_11 (and_11_out, P4, P3, G2);
  and and_12 (and_12_out, P4, P3, P2, G1);
  and and_13 (and_13_out, P4, P3, P2, P1, Cin);
  or or_1 (G_star, G4, and_1_out, and_2_out, and_3_out);
  or or_2 (C1, G1, and_5_out);
  or or_3 (or_3_out, G1, and_6_out);
  or or_4 (C3, G3, and_7_out, and_8_out, and_9_out);
  or or_5 (C4, G4, and_10_out, and_11_out, and_12_out, and_13_out);
  and and_14 (and_14_out, P2, or_3_out);
  or or_6 (C2, G2, and_14_out);
endmodule

module test (
  input  C0,
  input  X3,
  input  Y3,
  input  X2,
  input  Y2,
  input  X1,
  input  Y1,
  input  X0,
  input  Y0,
  output out_10,
  output C3,
  output S3,
  output S2,
  output S1,
  output S0,
  output G_star,
  output P_star,
  output C4
);

  wire and_1_out, and_2_out, and_3_out, and_4_out, \n4位先行进位电路_cla74182_1_c1 , \n4位先行进位电路_cla74182_1_c2 ,
       xor_1_out, xor_3_out, xor_5_out, xor_7_out;

  OF of_1 (.a(X3), .b(X3), .s(S3), .out_4(out_10));
  xor xor_1 (xor_1_out, X3, X3);
  and and_1 (and_1_out, X3, X3);
  xor xor_2 (S3, C3, xor_1_out);
  and and_2 (and_2_out, X2, Y2);
  xor xor_3 (xor_3_out, X2, Y2);
  xor xor_4 (S2, \n4位先行进位电路_cla74182_1_c2 , xor_3_out);
  and and_3 (and_3_out, X1, Y1);
  xor xor_5 (xor_5_out, X1, Y1);
  xor xor_6 (S1, \n4位先行进位电路_cla74182_1_c1 , xor_5_out);
  xor xor_7 (xor_7_out, X0, Y0);
  and and_4 (and_4_out, X0, Y0);
  xor xor_8 (S0, xor_7_out, C0);
  \_4位先行进位电路_CLA74182  \u_4位先行进位电路_cla74182_1  (
    .Cin(C0), .G1(and_4_out), .P1(xor_7_out), .G2(and_3_out), .P2(xor_5_out), .G3(and_2_out), .P3(xor_3_out),
    .G4(and_1_out), .P4(xor_1_out), .G_star(G_star), .P_star(P_star), .C1(\n4位先行进位电路_cla74182_1_c1 ),
    .C2(\n4位先行进位电路_cla74182_1_c2 ), .C3(C3), .C4(C4));

  assign Y3 = X3;
endmodule

module \原码一位乘法器  (
  input  [7:0] in_1,
  input  [7:0] in_2,
  output [15:0] out_3
);

  wire clock_1_out, comparator_1_eq, comparator_2_gt, not_1_out, RST, S;
  wire [0:0] \n8位串行加法器_1_out ;
  wire [7:0] counter_1_q, multiplexer_1_out, multiplexer_2_out, \n8位串行加法器_1_c ;
  wire [7:7] register_q;

  xor xor_1 (S, in_1[7], in_2[7]);
  Clock clock_1 (.out(clock_1_out));
  Button \u_复位  (.out(RST));
  // Probe on {register_q[7], out_3[14:8]}
  Register register (
    .D(\n8位串行加法器_1_c ), .en(not_1_out), .Q({register_q[7], out_3[14:8]}), .clk(clock_1_out), .clr(RST));
  \_8位串行加法器  \u_8位串行加法器_1  (
    .Out({\n8位串行加法器_1_c [6:0], \n8位串行加法器_1_out [0]}), .A({register_q[7], out_3[14:8]}),
    .B(multiplexer_1_out), .C(\n8位串行加法器_1_c [7]));
  Multiplexer #(.width(8), .disabled(0), .enable("false")) multiplexer_1 (
    .in0({8{1'b0}}), .in1({1'b0, in_1[6:0]}), .out(multiplexer_1_out), .sel(out_3[0]));
  Register Y (.D(multiplexer_2_out), .en(not_1_out), .Q(out_3[7:0]), .clk(clock_1_out), .clr(RST));
  Multiplexer #(.width(8), .enable("false")) multiplexer_2 (
    .in0({\n8位串行加法器_1_out [0], out_3[7:1]}), .in1({1'b0, in_2[6:0]}), .out(multiplexer_2_out),
    .sel(comparator_1_eq));
  // Probe on out_3[7:0]
  // Probe on in_1
  // Probe on out_3
  or or_1 (out_3[15], S, register_q[7]);
  Counter counter_1 (.count(not_1_out), .Q(counter_1_q), .clk(clock_1_out), .clr(RST));  // open: load, D, carry
  // Probe on in_2
  Comparator comparator_1 (.a(counter_1_q), .b({8{1'b0}}), .eq(comparator_1_eq));  // open: gt, lt
  Comparator comparator_2 (.a(counter_1_q), .b({8{1'b0}}), .gt(comparator_2_gt));  // open: eq, lt
  not not_1 (not_1_out, comparator_2_gt);

  // Other names for the same wires on the sheet: Product[15:0] = out_3; X[7:0] = in_1; X7 = in_1[7];
  //   X_u[6:0] = in_1[6:0]; Y[7:0] = in_2; Y7 = in_2[7]; Y_u[6:0] = in_2[6:0]

  // Notes on the sheet:
  //   8位原码1位乘法器
endmodule

// ADD
module \_8位串行加法器  (
  input  [7:0] A,
  input  [7:0] B,
  output [7:0] Out,
  output C
);

  wire n1_bit_fa_2_c, n1_bit_fa_3_c, n1_bit_fa_4_c, n1_bit_fa_5_c, n1_bit_fa_6_c, n1_bit_fa_7_c,
       n1_bit_fa_8_c;

  _1_bit_FA u_1_bit_fa_1 (.a(A[7]), .b(B[7]), .c_l(n1_bit_fa_2_c), .s(Out[7]), .c(C));
  _1_bit_FA u_1_bit_fa_2 (.a(A[6]), .b(B[6]), .c_l(n1_bit_fa_3_c), .s(Out[6]), .c(n1_bit_fa_2_c));
  _1_bit_FA u_1_bit_fa_3 (.a(A[5]), .b(B[5]), .c_l(n1_bit_fa_4_c), .s(Out[5]), .c(n1_bit_fa_3_c));
  _1_bit_FA u_1_bit_fa_4 (.a(A[4]), .b(B[4]), .c_l(n1_bit_fa_5_c), .s(Out[4]), .c(n1_bit_fa_4_c));
  _1_bit_FA u_1_bit_fa_5 (.a(A[3]), .b(B[3]), .c_l(n1_bit_fa_6_c), .s(Out[3]), .c(n1_bit_fa_5_c));
  _1_bit_FA u_1_bit_fa_6 (.a(A[2]), .b(B[2]), .c_l(n1_bit_fa_7_c), .s(Out[2]), .c(n1_bit_fa_6_c));
  _1_bit_FA u_1_bit_fa_7 (.a(A[1]), .b(B[1]), .c_l(n1_bit_fa_8_c), .s(Out[1]), .c(n1_bit_fa_7_c));
  _1_bit_FA u_1_bit_fa_8 (.a(A[0]), .b(B[0]), .c_l(1'b0), .s(Out[0]), .c(n1_bit_fa_8_c));
endmodule

module \RAM组件实验  (
  input  [2:0] \三位地址线 ,
  input  [7:0] \读出数据 ,
  input  in_3,
  input  in_4,
  output [7:0] out_5
);

  wire clock_1_out, not_1_out;
  wire [7:0] ram_1_data;

  Clock clock_1 (.out(clock_1_out));
  RAM #(.addrWidth(3)) ram_1 (.addr(\三位地址线 ), .data(ram_1_data), .sel(1'b1), .clk(clock_1_out), .ld(in_4), .clr(in_3));
  assign out_5 = in_4 ? ram_1_data : 8'bz;  // Controlled_Buffer controlled_buffer_1
  assign ram_1_data = not_1_out ? \读出数据  : 8'bz;  // Controlled_Buffer controlled_buffer_2
  not not_1 (not_1_out, in_4);

  // Notes on the sheet:
  //   要写入的数据
endmodule
